// Logisim project SA.circ as structural Verilog: 2 circuits, main circuit main
module main (
);

  wire clock_1_out, comparator_1_eq, comparator_1_gt, or_1_out, testcell_1_reset_thru, testcell_2_reset_thru,
       testcell_3_reset_thru, testcell_4_reset_thru, testcell_5_reset_thru, testcell_6_reset_thru,
       testcell_7_reset_thru;
  wire [4:0] counter_1_q;
  wire [7:0] register_1_q, testcell_8_dataout, testcell_8_testout;
  wire [17:0] rom_1_data;

  Clock clock_1 (.out(clock_1_out));
  Counter #(.width(5), .max('h11)) counter_1 (.Q(counter_1_q), .clk(clock_1_out));  // open: load, D, count, carry, clr
  TestCell testcell_1 (
    .Reset(rom_1_data[0]), .Test(rom_1_data[17]), .WRT(rom_1_data[16]), .DATA(or_1_out),
    .TestOut(testcell_8_testout[7]), .DataOut(testcell_8_dataout[7]), .Reset_Thru(testcell_1_reset_thru));
  ROM #(.addrWidth(5), .dataWidth(18)) rom_1 (.addr(counter_1_q), .data(rom_1_data));  // open: sel
  TestCell testcell_2 (
    .Reset(testcell_3_reset_thru), .Test(rom_1_data[13]), .WRT(rom_1_data[12]), .DATA(or_1_out),
    .TestOut(testcell_8_testout[5]), .DataOut(testcell_8_dataout[5]), .Reset_Thru(testcell_2_reset_thru));
  TestCell testcell_3 (
    .Reset(testcell_1_reset_thru), .Test(rom_1_data[15]), .WRT(rom_1_data[14]), .DATA(or_1_out),
    .TestOut(testcell_8_testout[6]), .DataOut(testcell_8_dataout[6]), .Reset_Thru(testcell_3_reset_thru));
  TestCell testcell_4 (
    .Reset(testcell_2_reset_thru), .Test(rom_1_data[11]), .WRT(rom_1_data[10]), .DATA(or_1_out),
    .TestOut(testcell_8_testout[4]), .DataOut(testcell_8_dataout[4]), .Reset_Thru(testcell_4_reset_thru));
  TestCell testcell_5 (
    .Reset(testcell_4_reset_thru), .Test(rom_1_data[9]), .WRT(rom_1_data[8]), .DATA(or_1_out),
    .TestOut(testcell_8_testout[3]), .DataOut(testcell_8_dataout[3]), .Reset_Thru(testcell_5_reset_thru));
  Comparator #(.mode("unsigned")) comparator_1 (
    .a(8'hca), .b(testcell_8_testout), .gt(comparator_1_gt), .eq(comparator_1_eq));  // open: lt
  TestCell testcell_6 (
    .Reset(testcell_7_reset_thru), .Test(rom_1_data[5]), .WRT(rom_1_data[4]), .DATA(or_1_out),
    .TestOut(testcell_8_testout[1]), .DataOut(testcell_8_dataout[1]), .Reset_Thru(testcell_6_reset_thru));
  TestCell testcell_7 (
    .Reset(testcell_5_reset_thru), .Test(rom_1_data[7]), .WRT(rom_1_data[6]), .DATA(or_1_out),
    .TestOut(testcell_8_testout[2]), .DataOut(testcell_8_dataout[2]), .Reset_Thru(testcell_7_reset_thru));
  or or_1 (or_1_out, comparator_1_gt, comparator_1_eq);
  TestCell testcell_8 (
    .Reset(testcell_6_reset_thru), .Test(rom_1_data[3]), .WRT(rom_1_data[2]), .DATA(or_1_out),
    .TestOut(testcell_8_testout[0]), .DataOut(testcell_8_dataout[0]));  // open: Reset_Thru
  LED led_1 (.in(or_1_out));
  Register register_1 (.D(testcell_8_dataout), .Q(register_1_q), .clk(rom_1_data[1]));  // open: en, clr
  // Probe on register_1_q

  // Notes on the sheet:
  //   VIN
  //   contents of rom_1 (hex, n*v repeats v):
  //   20000 30000 8000 c000 2000 3000 800 c00 200 300 80 c0 20 30 8 c 2 1
  //   "ANALOG SECTION"
  //   <- "DAC"
endmodule

module TestCell (
  input  Test,
  input  WRT,
  input  DATA,
  input  Reset,
  output Reset_Thru,
  output TestOut,
  output DataOut
);

  or or_1 (TestOut, Test, DataOut);
  D_Flip_Flop d_ff_1 (.clk(WRT), .D(DATA), .Q(DataOut), .reset(Reset));  // open: Qn, preset, en

  assign Reset_Thru = Reset;
endmodule
